# Fritzing sketch Untitled Sketch (saved by Fritzing 1.0.6)
circuit board: 9.68658cm x 5.73637cm
breadboards: 1

parts:
  M1 = DOIT Esp32 DevKit v1 (30 pins long, 11 pins width) [part_number=ESP32S-PIN30]
  M2 = gy9250
  J1 = female pin header, 4 pins [form="♀ (female)"]
  J44 = female pin header, 4 pins [form="♀ (female)"]
  J3 = female pin header, 4 pins [form="♀ (female)"]
  J4 = female pin header, 3 pins [form="♀ (female)"]
  J5 = female pin header, 3 pins [form="♀ (female)"]
  J6 = female pin header, 3 pins [form="♀ (female)"]
  J7 = female pin header, 3 pins [form="♀ (female)"]
  J8 = female pin header, 3 pins [form="♀ (female)"]
  Pad_- = Pad [width=7.902222222222222 height=9.03111111111111 connect=center]
  pad+ = Pad [width=7.902222222222222 height=9.03111111111111 connect=center]
  J11 = female pin header, 4 pins [form="♀ (female)"]
  J12 = female pin header, 1 pin [form="♀ (female)"]
  J13 = female pin header, 1 pin [form="♀ (female)"]
  J14 = female pin header, 1 pin [form="♀ (female)"]
  J15 = female pin header, 1 pin [form="♀ (female)"]
  J16 = female pin header, 1 pin [form="♀ (female)"]
  J17 = female pin header, 1 pin [form="♀ (female)"]
  J18 = female pin header, 1 pin [form="♀ (female)"]  # not connected
  J19 = female pin header, 1 pin [form="♀ (female)"]
  J20 = female pin header, 1 pin [form="♀ (female)"]  # not connected
  J21 = female pin header, 1 pin [form="♀ (female)"]  # not connected
  J22 = female pin header, 3 pins [form="♀ (female)"]
  J23 = female pin header, 1 pin [form="♀ (female)"]
  J24 = female pin header, 1 pin [form="♀ (female)"]
  J25 = female pin header, 1 pin [form="♀ (female)"]
  J26 = female pin header, 1 pin [form="♀ (female)"]
  J28 = female pin header, 1 pin [form="♀ (female)"]
  J29 = female pin header, 1 pin [form="♀ (female)"]  # not connected
  J30 = female pin header, 1 pin [form="♀ (female)"]  # not connected
  J31 = female pin header, 1 pin [form="♀ (female)"]  # not connected
  J32 = female pin header, 1 pin [form="♀ (female)"]  # not connected
  J33 = female pin header, 1 pin [form="♀ (female)"]  # not connected
  J34 = female pin header, 1 pin [form="♀ (female)"]  # not connected
  Pad1 = Pad [width=2.2927543520157387 height=1.7982292643067856 connect=center]  # not connected
  Pad3 = Pad [width=2.2927543520157387 height=1.7982292643067856 connect=center]  # not connected
  Pad4 = Pad [width=2.2927543520157387 height=1.7982292643067856 connect=center]  # not connected
  Pad5 = Pad [width=2.2927543520157387 height=1.7982292643067856 connect=center]  # not connected
  Pad6 = Pad [width=2.2927543520157387 height=1.7982292643067856 connect=center]  # not connected
  Pad7 = Pad [width=2.2927543520157387 height=1.7982292643067856 connect=center]  # not connected
  Pad8 = Pad [width=2.2927543520157387 height=1.7982292643067856 connect=center]  # not connected
  Pad9 = Pad [width=2.2927543520157387 height=1.7982292643067856 connect=center]  # not connected
  J37 = female pin header, 1 pin [form="♀ (female)"]  # not connected
  J35 = female pin header, 1 pin [form="♀ (female)"]  # not connected
  J38 = female pin header, 1 pin [form="♀ (female)"]  # not connected
  J43 = female pin header, 1 pin [form="♀ (female)"]  # not connected
  J45 = female pin header, 4 pins [form="♀ (female)"]

nets:
  N1: M1.3V3, M2.pin2, J45.pin4
  N2: M1.GND, M2.pin3, J1.pin1, J44.pin2, J3.pin2, J4.pin3, J5.pin3, J6.pin3, J7.pin3, J8.pin3, J11.pin1, J16.pin1, J17.pin1, J19.pin1, J22.pin3, J28.pin1, J45.pin3
  N3: M1.D4, M2.pin4, J45.pin2
  N4: M1.RX2, J1.pin4
  N5: M1.TX2, J1.pin3
  N6: M1.D18, M2.pin5, J45.pin1
  N7: M1.D19, J44.pin4
  N8: M1.D21, J44.pin3
  N9: M1.D22, J3.pin4
  N10: M1.D23, J3.pin3
  N11: M1.D35, J12.pin1, J15.pin1, J23.pin1
  N12: M1.D32, J4.pin1
  N13: M1.D33, J8.pin1
  N14: M1.D25, J22.pin1
  N15: M1.D26, J7.pin1
  N16: M1.D27, J5.pin1
  N17: M1.D13, J6.pin1
  N18: J1.pin2, J26.pin1
  N19: J44.pin1, J3.pin1, J4.pin2, J5.pin2, J6.pin2, J7.pin2, J8.pin2, J11.pin2, J22.pin2
  N20: Pad_-.pad, J11.pin4, J13.pin1, J25.pin1
  N21: pad+.pad, J11.pin3, J14.pin1, J24.pin1

notes:
  ESP32
  MPU9250
  +
  -
  VECIHI
  s
  3.3
  gnd
  scl
  sda
  GPS
  recv
  BEC 1
  BEC 2
  CAM
  airspd

custom parts:
  DOIT Esp32 DevKit v1 (30 pins long, 11 pins width): The DOIT Esp32 DevKit v1 is one of the development board created by DOIT to evaluate the ESP-WROOM-32 module. It is based on the ESP32 microcontroller that boasts Wifi, Bluetooth, Ethernet and Low Power support all in a single chip. (vanepp) made breadboard work, adjusted pin numbering and labels and reduced size of schematic and cleaned up pcb. This chip is 30pins long (2 x15) and 11 pins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
  gy9250: MPU-9250 module (three-axis gyroscope + three-axis acceleration + three-axis magnetic field). The generic model from ebay et. al. rather than the Sparkfun version.
